# Fritzing sketch VCNL4040 Wiring (saved by Fritzing 0.9.3b)

parts:
  Bauteil1 = Arduino Uno (Rev3)
  Level_Converter_3_3_<->_5V = Logic Level Converter
  R1/R2 = Resistor [tolerance=±5% resistance=4.7k package=THT]
  R3 = Resistor [tolerance=±5% resistance=10k package=THT]
  R2 = Resistor [tolerance=±5% resistance=4.7k package=THT]

nets:
  N1: Bauteil1.A4/SDA, Level_Converter_3_3_<->_5V.RX2_LV, R2.Pin_1
  N2: Bauteil1.A5/SCL, Level_Converter_3_3_<->_5V.TX2_LV, R1/R2.Pin_1
  GND: Bauteil1.GND, Level_Converter_3_3_<->_5V.GND
  N3: Bauteil1.D2, Level_Converter_3_3_<->_5V.RX_LV, R3.Pin_1
  N4: Bauteil1.3V3, Level_Converter_3_3_<->_5V.LV, R1/R2.Pin_0, R3.Pin_0, R2.Pin_0
  N5: Bauteil1.5V, Level_Converter_3_3_<->_5V.HV
